# Fritzing sketch SCARA (saved by Fritzing 0.8.7b)

parts:
  Part2 = Arduino Mega 2560 (Rev3)
  MD09B1 = A4988 Stepper Motor Driver Carrier
  MD09B2 = A4988 Stepper Motor Driver Carrier
  MD09B3 = A4988 Stepper Motor Driver Carrier
  Part3 = RAMPS 1.4 Shield for Arduino Mega 2560
  MD09B4 = A4988 Stepper Motor Driver Carrier
  D2F1 = D2F-FL Omron Snap Action Limit Switch with Level
  D2F2 = D2F-FL Omron Snap Action Limit Switch with Level
  D2F3 = D2F-FL Omron Snap Action Limit Switch with Level
  M2 = Stepper Motor - Bipolar
  M3 = Stepper Motor - Bipolar
  M4 = Stepper Motor - Bipolar
  M5 = Stepper Motor - Bipolar

nets:
  N1: Part2.D21/SCL, Part3.5V/ZMIN_ENDSTOP
  N2: Part2.D20/SDA, Part3.5V/YMAX_ENDSTOP
  N3: Part2.D19/RX1, Part3.5V/YMIN_ENDSTOP
  N4: Part2.D18/TX1, Part3.5V/XMAX_ENDSTOP
  N5: Part2.D17_PWM/RX2, Part3.D20/SDA, Part3.5V/XMIN_ENDSTOP
  N6: Part2.D6_PWM, MD09B4.GROUND
  N7: Part2.D7_PWM, MD09B4.VDD
  N8: Part2.D40, MD09B3.GROUND
  N9: Part2.D50, MD09B3.DIR
  N10: MD09B1.Enable, Part3.D38/X_EN
  N11: MD09B1.DIR, Part3.D55/X_DIR
  N12: MD09B2.STEP, Part3.D60/Y_STEP
  N13: MD09B2.DIR, Part3.D61/Y_DIR
  N14: MD09B3.Enable, Part3.D62/Z_EN
  N15: Part3.D18/ZMIN_ENDSTOP, D2F3.COM
  N16: Part3.D14/YMIN_ENDSTOP, D2F2.COM
  N17: Part3.D3/XMIN_ENDSTOP, D2F1.COM
  N18: Part3.GND/XMIN_ENDSTOP, D2F1.NC
  N19: Part3.GND/YMIN_ENDSTOP, D2F2.NC
  N20: Part3.GND/ZMIN_ENDSTOP, D2F3.NC
  N21: Part3.E0_2B, M5.A
  N22: Part3.E0_2A, M5.C
  N23: Part3.E0_1A, M5.B
  N24: Part3.E0_1B, M5.D
  N25: Part3.X_2B, M4.D
  N26: Part3.X_2A, M4.B
  N27: Part3.X_1A, M4.C
  N28: Part3.X_1B, M4.A
  N29: Part3.Y_2B, M3.D
  N30: Part3.Y_2A, M3.B
  N31: Part3.Y_1A, M3.C
  N32: Part3.Y_1B, M3.A
  N33: Part3.Z_TOP_2B, M2.D
  N34: Part3.Z_TOP_2A, M2.B
  N35: Part3.Z_TOP_1A, M2.C
  N36: Part3.Z_TOP_1B, M2.A

custom parts:
  RAMPS 1.4 Shield for Arduino Mega 2560: This ia standard Ramps 1.4 shield which is also compatible with versions 1.5 and 1.6 of the Ramps board. This model is intended only for the breadboard view, as the schematic and PCB views are not entirely accurate.
  D2F-FL Omron Snap Action Limit Switch with Level: Snap action switch with stainless steel lever.
